# Fritzing sketch client (saved by Fritzing 0.8.3b)
breadboards: 1

parts:
  Part1 = Arduino Uno (Rev3)
  NRF24L1 = NRF24L01
  LED1 = LEDs [package=led10mm]
  LED2 = LEDs [package=led10mm]
  LED3 = LEDs [package=led10mm]

nets:
  GND: Part1.GND, NRF24L1.GND, LED1.A, LED2.A, LED3.A
  N1: Part1.D8, NRF24L1.CE
  N2: Part1.D11_PWM/MOSI, NRF24L1.MOSI
  N3: Part1.D12/MISO, NRF24L1.MISO
  N4: Part1.D13/SCK, NRF24L1.SCK
  N5: Part1.D2, LED1.C
  N6: Part1.D4, LED2.C
  N7: Part1.D6_PWM, LED3.C
  N8: Part1.D7, NRF24L1.CSN
  3V3: Part1.3V3, NRF24L1.VCC

notes:
  Device 2
  Device 1
  Device 3

custom parts:
  NRF24L01: NRF24L01 module
