# Fritzing sketch server (saved by Fritzing 0.8.3b)

parts:
  NRF24L1 = NRF24L01
  Part1 = Arduino Uno (Rev3)

nets:
  VCC: NRF24L1.VCC, Part1.3V3
  N1: NRF24L1.CSN, Part1.D7
  N2: NRF24L1.MOSI, Part1.D11_PWM/MOSI
  GND: NRF24L1.GND, Part1.GND
  N3: NRF24L1.CE, Part1.D8
  N4: NRF24L1.SCK, Part1.D13/SCK
  N5: NRF24L1.MISO, Part1.D12/MISO

custom parts:
  NRF24L01: NRF24L01 module
